# Fritzing sketch poor-man-can (saved by Fritzing 0.9.2b)
breadboards: 1

parts:
  Transmitter = Photon
  Receiver = Photon
  S1 = Pushbutton [package="[THT]"]
  U1 = SN74LS21N [package="DIP14 [THT]"]
  LED1 = LED - 5mm [color="Green (560nm)" package="5 mm [THT]"]
  R1 = Resistor [tolerance=±5% resistance=220 package=THT]

nets:
  N1: Transmitter.D1, U1.1A
  N2: Transmitter.D2, Receiver.D2, U1.1Y
  N3: Transmitter.D4, S1.Pin_3, S1.Pin_4
  N4: Transmitter.D6, S1.Pin_1, S1.Pin_2
  N5: Receiver.A3, LED1.cathode
  N6: Receiver.DAC, R1.Pin_0
  GND: Receiver.GND, U1.GND
  VIN: Receiver.VIN, U1.1C, U1.1D, U1.VCC
  N7: Receiver.D1, U1.1B
  N8: LED1.anode, R1.Pin_1

notes:
  Yellow: Fake CAN bus
  Green: CAN TX signals
